# Fritzing sketch led_cube_sch (saved by Fritzing 0.9.3b)
breadboards: 1

parts:
  LED1 = LED - 5mm [color="Green (555nm)" package="5 mm [THT]"]
  LED2 = LED - 5mm [color="Green (555nm)" package="5 mm [THT]"]
  LED3 = LED - 5mm [color="Green (555nm)" package="5 mm [THT]"]
  LED4 = LED - 5mm [color="Green (555nm)" package="5 mm [THT]"]
  LED5 = LED - 5mm [color="Green (555nm)" package="5 mm [THT]"]
  LED6 = LED - 5mm [color="Green (555nm)" package="5 mm [THT]"]
  LED7 = LED - 5mm [color="Green (555nm)" package="5 mm [THT]"]
  LED8 = LED - 5mm [color="Green (555nm)" package="5 mm [THT]"]
  R1 = Resistor [tolerance=±5% resistance=680 package=THT]
  R2 = Resistor [tolerance=±5% resistance=680 package=THT]
  R3 = Resistor [tolerance=±5% resistance=680 package=THT]
  R4 = Resistor [tolerance=±5% resistance=680 package=THT]
  U1 = NodeMCU V1.0

nets:
  N1: LED1.cathode, LED2.cathode, LED3.cathode, LED4.cathode, U1.D3
  N2: LED1.anode, LED6.anode, R1.Pin_1
  N3: LED2.anode, LED5.anode, R4.Pin_0
  N4: LED3.anode, LED8.anode, R3.Pin_1
  N5: LED4.anode, LED7.anode, R2.Pin_0
  N6: LED5.cathode, LED6.cathode, LED7.cathode, LED8.cathode, U1.D2
  N7: R1.Pin_0, U1.D8
  N8: R2.Pin_1, U1.D5
  N9: R3.Pin_0, U1.D6
  N10: R4.Pin_1, U1.D7

custom parts:
  NodeMCU V1.0: ESP8266 based NodeMCU
