# Fritzing sketch key_matrix (saved by Fritzing 0.9.2b)
breadboards: 1

parts:
  S2 = Pushbutton [package=THT]
  Part1 = Arduino Uno (Rev3)
  S3 = Pushbutton [package=THT]
  S4 = Pushbutton [package=THT]
  S1 = Pushbutton [package=THT]

nets:
  N1: S2.leg0, Part1.D2, S1.leg0
  N2: S2.leg1, Part1.D12/MISO, S4.leg1
  N3: Part1.D11_PWM/MOSI, S3.leg1, S1.leg1
  N4: Part1.D3_PWM, S3.leg0, S4.leg0
