# Fritzing sketch key_matrix_diode (saved by Fritzing 0.9.2b)
breadboards: 1

parts:
  S2 = Pushbutton [package=THT]
  Part1 = Arduino Uno (Rev3)
  S3 = Pushbutton [package=THT]
  S4 = Pushbutton [package=THT]
  S1 = Pushbutton [package=THT]
  D1 = Diode [package=diode-1n4001]
  D2 = Diode [package=diode-1n4001]
  D3 = Diode [package=diode-1n4001]
  D4 = Diode [package=diode-1n4001]

nets:
  N1: S2.leg0, Part1.D2, S1.leg0
  N2: S2.leg1, D2.A
  N3: Part1.D11_PWM/MOSI, D1.C, D3.C
  N4: Part1.D12/MISO, D2.C, D4.C
  N5: Part1.D3_PWM, S3.leg0, S4.leg0
  N6: S3.leg1, D3.A
  N7: S4.leg1, D4.A
  N8: S1.leg1, D1.A
