# Fritzing sketch Arduino_I2C (saved by Fritzing 0.9.3b)

parts:
  Part1 = Arduino Uno (Rev3)
  Part2 = Arduino Uno (Rev3)

nets:
  N1: Part1.A4/SDA, Part2.A4/SDA
  N2: Part1.A5/SCL, Part2.A5/SCL
  GND: Part1.GND, Part2.GND
  5V: Part1.5V, Part2.5V
