# Fritzing sketch schematic (saved by Fritzing 0.9.2b)

parts:
  Part1 = Arduino Uno (Rev3)
  C1 = Electrolytic Capacitor [capacitance=47µF package="100 mil [THT, electrolytic]"]
  SPKR1 = Loudspeaker
  S1 = Round Pushbutton
  S2 = Round Pushbutton

nets:
  N1: Part1.D9_PWM, C1.+
  N2: Part1.D10_PWM/SS, S2.leg1
  N3: Part1.D11_PWM/MOSI, S1.leg1
  N4: Part1.GND, SPKR1.pin1
